# Fritzing sketch Circuit (saved by Fritzing 0.9.3b)
breadboards: 1

parts:
  C1 = Electrolytic Capacitor [capacitance=1µF package="100 mil [THT, electrolytic]"]
  U1 = LIPO-110mAh [package=lipo-110]
  Q1 = NPN-Transistor [package="TO92 [THT]"]  # not connected
  Handy = screw terminal, 2 pins  # not connected
  GSM_SIM_GPSR_SMS_SIM900_SIM1 = SIM800L [package=THT]
  U3 = Voltage Regulator - 5V [package="TO220 [THT]"]  # not connected
  R1 = Resistor [tolerance=±5% resistance=10k package="2010 [SMD]"]  # not connected
  C7 = Capacitor [package=cap-pth-small]  # not connected
  C10 = Ceramic Capacitor [capacitance="100 nF" package="0603 [SMD, multilayer]"]  # not connected
  Handy1 = screw terminal, 2 pins  # not connected
  Handy2 = screw terminal, 2 pins  # not connected
  Handy3 = screw terminal, 2 pins  # not connected
  Bauteil1 = Arduino Nano (Rev3.0) (ICSP)
  VCC1 = Battery block 9V  # not connected
  TP1 = TP4056 [chip_label=TP4056 package="DIP (Dual Inline) [THT]"]

nets:
  GND: C1.-, GSM_SIM_GPSR_SMS_SIM900_SIM1.GND, Bauteil1.GND, TP1.pin6
  VDD: C1.+, GSM_SIM_GPSR_SMS_SIM900_SIM1.VDD, Bauteil1.VIN, TP1.pin3
  N1: U1.+, TP1.pin4
  N2: U1.-, TP1.pin5
  N3: GSM_SIM_GPSR_SMS_SIM900_SIM1.SIM_TXD, Bauteil1.A5
  N4: GSM_SIM_GPSR_SMS_SIM900_SIM1.SIM_RXD, Bauteil1.A4

custom parts:
  TP4056: A DIP stand-in part for whatever IC you want. With 6 pins on a 300mil dual inline package (DIP) footprint.
